# Fritzing sketch nixie-driver-v1 (saved by Fritzing 0.9.2b)
circuit board: 10cm x 6cm
circuit board: 6.8958cm x 4.98785cm
perfboards: 2

parts:
  R20 = Resistor [tolerance=±5% resistance=68k package=THT]
  Q11 = NPN-Transistor [part_number=MPSA42 package="TO92 [THT]"]
  R21 = Resistor [tolerance=±5% resistance=68k package=THT]
  Q12 = NPN-Transistor [part_number=MPSA42 package="TO92 [THT]"]
  J24_(IN-12_cathodes) = male pin header, 10 pins [form="♂ (male)"]
  U1 = TLP621 [package=THT]
  U2 = TLP621 [package=THT]
  U3 = TLP621 [package=THT]
  U4 = TLP621 [package=THT]
  R22 = Resistor [tolerance=±5% resistance=2.2k package=THT]
  HCTN541N = IC, DIP package, 20 pins [chip_label=HCT541N]
  Raspberry_Pi1 = Raspberry Pi 2
  IC5 = K155ID1 [part_number=K155ID1 chip_label=K155ID1 package="DIP (Dual Inline) [THT]"]
  R23 = Resistor [tolerance=±5% resistance=47k package=THT]
  R24 = Resistor [tolerance=±5% resistance=47k package=THT]
  Composant1 = MPR121 Breakout
  PEC11R1 = PEC11R [chip_label=PEC11R package=THT]
  R25 = Resistor [tolerance=±5% resistance=10k package=THT]
  R26 = Resistor [tolerance=±5% resistance=10k package=THT]
  R27 = Resistor [tolerance=±5% resistance=10k package=THT]
  R28 = Resistor [tolerance=±5% resistance=10k package=THT]
  C1 = Ceramic Capacitor [capacitance=100nF package="100 mil [THT, multilayer]"]
  C2 = Ceramic Capacitor [capacitance=100nF package="100 mil [THT, multilayer]"]
  C3 = Ceramic Capacitor [capacitance=10nF package="100 mil [THT, multilayer]"]
  R29 = Resistor [tolerance=±5% resistance=10k package=THT]
  Q13 = NPN-Transistor [part_number=2N3904 package="TO92 [THT]"]
  R30 = Resistor [tolerance=±5% resistance=2.2k package=THT]
  MT2_C1 = DIP - 16 pins [chip_label="MT2 C93401" package="DIP (Dual Inline) [THT]"]
  U5 = CAPSENSE_PAD [package=capsense_pad]
  U6 = CAPSENSE_PAD [package=capsense_pad]
  U7 = CAPSENSE_PAD [package=capsense_pad]
  J9_(voice_transformer) = female pin header, 2 pins [form="♀ (female)"]
  R32 = Resistor [tolerance=±5% resistance=330k package=THT]
  R33 = Resistor [tolerance=±5% resistance=330k package=THT]
  D3 = Rectifier Diode [part_number=1N4001 package="300 mil [THT]"]
  J5 = female pin header, 8 pins [form="♀ (female)"]
  J4 = female pin header, 8 pins [form="♀ (female)"]
  J10_(SPKR_coil) = female pin header, 2 pins [form="♀ (female)"]
  J7_(filter_coil) = female pin header, 2 pins [form="♀ (female)"]
  J20_(HV_supply_out) = female pin header, 2 pins [form="♀ (female)"]
  J21_(HV_supply_in) = female pin header, 3 pins [form="♀ (female)"]
  J6_(12V_supply) = female pin header, 2 pins [form="♀ (female)"]
  J26_(INS-1) = female pin header, 2 pins [form="♀ (female)"]
  J27_(INS-1) = female pin header, 2 pins [form="♀ (female)"]
  J23_(IN-12_anodes) = female pin header, 4 pins [form="♀ (female)"]
  J22_(12V_in) = female pin header, 2 pins [form="♀ (female)"]
  U9 = TLP621 [package=THT]
  R35 = Resistor [tolerance=±5% resistance=2.2k package=THT]
  J3 = female pin header, 11 pins [form="♀ (female)"]
  J11_(PAM8403_out) = female pin header, 2 pins [form="♀ (female)"]
  J12_(PAM8403_PWR) = female pin header, 2 pins [form="♀ (female)"]
  J25 = female pin header, 11 pins [form="♀ (female)"]
  J14_(audio_in) = female pin header, 2 pins [form="♀ (female)"]
  J13_(PAM8403_in) = female pin header, 3 pins [form="♀ (female)"]
  D2 = Rectifier Diode [part_number=1N4001 package="300 mil [THT]"]
  J15 = male pin header, 3 pins [form="♂ (male)"]
  J16 = male pin header, 3 pins [form="♂ (male)"]
  J8(radio_HV) = female pin header, 2 pins [form="♀ (female)"]
  J1 = female pin header, 20 pins [form="♀ (female)"]
  J2 = female pin header, 20 pins [form="♀ (female)"]
  MT2_C2 = DIP - 16 pins [chip_label="MT2 C93401" package="DIP (Dual Inline) [THT]"]
  R36 = Resistor [tolerance=±5% resistance=1.5k package=THT]
  Pad1 = Pad [width=2.17472385845383 height=2.37915603911928 connect=center]
  Pad2 = Pad [width=2.17472385845383 height=2.37915603911928 connect=center]
  Pad3 = Pad [width=2.17472385845383 height=2.37915603911928 connect=center]
  Pad4 = Pad [width=2.17472385845383 height=2.37915603911928 connect=center]
  Pad5 = Pad [width=2.17472385845383 height=2.37915603911928 connect=center]
  Pad6 = Pad [width=2.17472385845383 height=2.37915603911928 connect=center]

nets:
  N1: R20.Pin_0, HCTN541N.pin12, J3.pin9, J25.pin9
  N2: R20.Pin_1, Q11.B
  GND: Q11.E, Q12.E, HCTN541N.pin10, Raspberry_Pi1.GND, IC5.GND, Composant1.GND, PEC11R1.SW2, PEC11R1.TC, C1.0, C2.0, C3.0, Q13.E, J5.pin5, J4.pin5, J20_(HV_supply_out).pin2, U9.Pin_2, J3.pin11, J12_(PAM8403_PWR).pin1, J25.pin11, J15.pin1, J1.pin5, J1.pin13, J1.pin20, J2.pin3, J2.pin7, J2.pin10, J2.pin15, Pad5.pad
  N3: Q11.C, J26_(INS-1).pin2
  N4: R21.Pin_0, HCTN541N.pin11, J3.pin10, J25.pin10
  N5: R21.Pin_1, Q12.B
  N6: Q12.C, J27_(INS-1).pin2
  N7: J24_(IN-12_cathodes).pin1, IC5.0
  N8: J24_(IN-12_cathodes).pin2, IC5.1
  N9: J24_(IN-12_cathodes).pin3, IC5.5
  N10: J24_(IN-12_cathodes).pin4, IC5.4
  N11: J24_(IN-12_cathodes).pin5, IC5.8
  N12: J24_(IN-12_cathodes).pin6, IC5.6
  N13: J24_(IN-12_cathodes).pin7, IC5.7
  N14: J24_(IN-12_cathodes).pin8, IC5.3
  N15: J24_(IN-12_cathodes).pin9, IC5.9
  N16: J24_(IN-12_cathodes).pin10, IC5.2
  N17: U1.Pin_1, U2.Pin_2, Raspberry_Pi1.GPIO7, J3.pin4, J25.pin4, J2.pin13
  N18: U1.Pin_2, U2.Pin_1, U3.Pin_2, U4.Pin_1, R22.Pin_1
  N19: U1.Pin_4, U2.Pin_4, R23.Pin_0
  N20: U1.Pin_3, J23_(IN-12_anodes).pin2
  N21: U2.Pin_3, J23_(IN-12_anodes).pin1
  N22: U3.Pin_1, U4.Pin_2, Raspberry_Pi1.GPIO8, J3.pin3, J25.pin3, J2.pin12
  N23: U3.Pin_4, U4.Pin_4, R24.Pin_0
  N24: U3.Pin_3, J23_(IN-12_anodes).pin3
  N25: U4.Pin_3, J23_(IN-12_anodes).pin4
  N26: R22.Pin_0, Raspberry_Pi1.GPIO25, J3.pin2, J25.pin2, J2.pin11
  N27: HCTN541N.pin4, Raspberry_Pi1.GPIO10, J1.pin10
  N28: HCTN541N.pin5, Raspberry_Pi1.GPIO9, J1.pin11
  N29: HCTN541N.pin6, Raspberry_Pi1.GPIO18, J2.pin6
  N30: HCTN541N.pin7, Raspberry_Pi1.GPIO11, J1.pin12
  N31: HCTN541N.pin8, Raspberry_Pi1.GPIO23, J2.pin8
  N32: HCTN541N.pin9, Raspberry_Pi1.GPIO24, J2.pin9
  N33: HCTN541N.pin13, IC5.C, J3.pin8, J25.pin8
  N34: HCTN541N.pin14, IC5.B, J3.pin7, J25.pin7
  N35: HCTN541N.pin15, IC5.D, J3.pin6, J25.pin6
  N36: HCTN541N.pin16, IC5.A, J3.pin5, J25.pin5
  5V: HCTN541N.pin20, Raspberry_Pi1.5V, IC5.VCC, MT2_C1.C2, J3.pin1, J12_(PAM8403_PWR).pin2, J25.pin1, D2.cathode, J15.pin3, J2.pin1, J2.pin2, MT2_C2.C2, R36.Pin_1, Pad3.pad
  3.3V: Raspberry_Pi1.3v3, Raspberry_Pi1.3V3, Composant1.3.3V, R27.Pin_0, R28.Pin_0, J5.pin1, J4.pin1, J1.pin1, Pad4.pad
  N37: Raspberry_Pi1.GPIO2, Composant1.SDA, J5.pin2, J4.pin2, J1.pin2
  N38: Raspberry_Pi1.GPIO3, Composant1.SCL, J5.pin3, J4.pin3, J1.pin3
  N39: Raspberry_Pi1.GPIO4, Composant1.~IRQ, J5.pin4, J4.pin4, J1.pin4
  N40: Raspberry_Pi1.GPIO17, R25.Pin_0, C2.1, J1.pin6
  N41: Raspberry_Pi1.GPIO27, R26.Pin_0, C1.1, J1.pin7
  N42: Raspberry_Pi1.GPIO22, C3.1, R29.Pin_0, J1.pin8
  N43: Raspberry_Pi1.ID_SD, J1.pin14
  N44: Raspberry_Pi1.GPIO5, J1.pin15
  N45: Raspberry_Pi1.GPIO6, J1.pin16
  N46: Raspberry_Pi1.GPIO13, J1.pin17
  N47: Raspberry_Pi1.GPIO19, J1.pin18
  N48: Raspberry_Pi1.GPIO26, J1.pin19
  N49: Raspberry_Pi1.GPIO21, J2.pin20
  N50: Raspberry_Pi1.GPIO20, J2.pin19
  N51: Raspberry_Pi1.GPIO16, J2.pin18
  N52: Raspberry_Pi1.GPIO12, J16.pin1, J2.pin16
  N53: Raspberry_Pi1.ID_SC, J2.pin14
  N54: Raspberry_Pi1.GPIO15, J2.pin5
  N55: Raspberry_Pi1.GPIO14, J2.pin4
  170V: R23.Pin_1, R24.Pin_1, R32.Pin_1, R33.Pin_1, J20_(HV_supply_out).pin1
  N56: Composant1.ELE8, U7.RECEIVE
  N57: Composant1.ELE4, U6.RECEIVE
  N58: Composant1.ELE0, U5.RECEIVE
  N59: PEC11R1.SW1, R29.Pin_1, J5.pin8, J4.pin8
  N60: PEC11R1.TA, R25.Pin_1, R27.Pin_1, J5.pin6, J4.pin6
  N61: PEC11R1.TB, R26.Pin_1, R28.Pin_1, J5.pin7, J4.pin7
  N62: Q13.B, R30.Pin_1
  N63: Q13.C, MT2_C1.C1, D2.anode, MT2_C2.C1
  N64: R30.Pin_0, J15.pin2, Pad2.pad
  N65: MT2_C1.NC1, J11_(PAM8403_out).pin2
  N66: MT2_C1.COM1, J10_(SPKR_coil).pin2
  N67: MT2_C1.NO1, J9_(voice_transformer).pin2
  N68: MT2_C1.NO2, J9_(voice_transformer).pin1
  N69: MT2_C1.COM2, J10_(SPKR_coil).pin1
  N70: MT2_C1.NC2, J11_(PAM8403_out).pin1
  N71: R32.Pin_0, J27_(INS-1).pin1
  N72: R33.Pin_0, J26_(INS-1).pin1
  12V: D3.cathode, J21_(HV_supply_in).pin1, J6_(12V_supply).pin2, J22_(12V_in).pin1, MT2_C2.NC2, Pad6.pad
  N73: D3.anode, U9.Pin_4, MT2_C2.NC1
  N74: J7_(filter_coil).pin1, MT2_C2.COM2
  N75: J7_(filter_coil).pin2, MT2_C2.COM1
  0V: J21_(HV_supply_in).pin3, J6_(12V_supply).pin1, J22_(12V_in).pin2, U9.Pin_3
  N76: U9.Pin_1, R35.Pin_1
  N77: R35.Pin_0, J16.pin2, Pad1.pad
  N78: J14_(audio_in).pin1, J13_(PAM8403_in).pin2
  N79: J14_(audio_in).pin2, J13_(PAM8403_in).pin1
  N80: J16.pin3, R36.Pin_0
  N81: J8(radio_HV).pin1, MT2_C2.NO2
  N82: J8(radio_HV).pin2, MT2_C2.NO1

notes:
  TODO: check nixie with PWM an 1mA current/47kOhm (fast enough switching?)
  5V
  3.3
  GND
  12V supply
  12V
  SPKR
  RDIO
  Pi
  Pi_sel
  Amp
  +
  filter
  Rdio HV
  TA
  TB
  SW
  SDA
  SCL
  IRQ
  DOTS
  CATHODES
  ANODES
  R
  L

custom parts:
  K155ID1: A DIP stand-in part for whatever IC you want. With 16 pins on a 300mil dual inline package (DIP) footprint.
  PEC11R: A dummy, proxy, ersatz, stand-in part for whatever you want. With 5 pins on a 100 mil inline pin header footprint.
  DIP - 16 pins: DPDT relay in DIP16 format.
